// Logisim project main.circ as structural Verilog: 3 circuits, main circuit main
module main (
);

  wire button_1_out, button_2_out, clock_1_out, controlador_auto_1_out_4, controlador_auto_1_out_5,
       controlador_auto_1_out_7, controlador_auto_1_verde, controlador_peaton_1_rojo,
       controlador_peaton_1_verde, not_1_out, or_1_out, or_2_out, or_3_out, or_4_out, or_5_out;

  Button button_1 (.out(button_1_out));
  not not_1 (not_1_out, button_1_out);
  Button button_2 (.out(button_2_out));
  Clock clock_1 (.out(clock_1_out));
  controlador_auto controlador_auto_1 (
    .Clock(clock_1_out), .Reset(not_1_out), .in_3(button_2_out), .out_4(controlador_auto_1_out_4),
    .out_5(controlador_auto_1_out_5), .Verde(controlador_auto_1_verde), .out_7(controlador_auto_1_out_7));
  controlador_peaton controlador_peaton_1 (
    .Clock(clock_1_out), .Reset(not_1_out), .Ctrl___Auto(controlador_auto_1_out_7),
    .Rojo(controlador_peaton_1_rojo), .Verde(controlador_peaton_1_verde));
  or or_1 (or_1_out, button_1_out, controlador_auto_1_out_4);
  or or_2 (or_2_out, button_1_out, controlador_auto_1_out_5);
  or or_3 (or_3_out, button_1_out, controlador_auto_1_verde);
  or or_4 (or_4_out, button_1_out, controlador_peaton_1_rojo);
  or or_5 (or_5_out, button_1_out, controlador_peaton_1_verde);
  LED led_1 (.in(or_1_out));
  LED led_2 (.in(or_2_out));
  LED led_3 (.in(or_3_out));
  LED led_4 (.in(or_4_out));
  LED led_5 (.in(or_5_out));

  // Notes on the sheet:
  //   Reset
  //   Boton Peaton
  //   ROJO AUTO
  //   AMARILLO AUTO
  //   VERDE AUTO
  //   ROJO PEATON
  //   VERDE PEATON
endmodule

// auto
module controlador_auto (
  input  Clock,
  input  Reset,
  input  in_3,
  output out_4,
  output out_5,
  output Verde,
  output out_7
);

  or or_1 (out_7, Clock, Reset, in_3);
  not not_1 (out_4, out_7);
  not not_2 (out_5, out_7);

  assign Verde = out_7;

  // Notes on the sheet:
  //   Boton - Peaton
  //   Controlador Peaton
  //   Rojo
  //   Amarillo
endmodule

// peaton
module controlador_peaton (
  input  Clock,
  input  Reset,
  input  Ctrl___Auto,
  output Rojo,
  output Verde
);

  or or_1 (Rojo, Clock, Reset, Ctrl___Auto);
  not not_1 (Verde, Rojo);
endmodule
